// Logisim project mips_processor.circ as structural Verilog
module IMEM (
  input  [31:0] BranchAddress,
  input  PCSRC,
  input  CLK,
  output [31:0] INSTRUCTION
);

  wire not_1_out, not_2_out, not_3_out, not_4_out, not_5_out, not_6_out, not_7_out, not_8_out, not_9_out;
  wire [23:0] PC_q_2;
  wire [31:0] adder_1_out, multiplexer_1_out, PC_q, ram_1_data, ram_2_data, ram_3_data, ram_4_data;

  Multiplexer #(.width(32)) multiplexer_1 (
    .in0(adder_1_out), .in1(BranchAddress), .out(multiplexer_1_out), .sel(PCSRC), .en(1'b1));
  not not_1 (not_1_out, 1'b0);
  not not_2 (not_2_out, 1'b0);
  not not_3 (not_3_out, 1'b0);
  not not_4 (not_4_out, 1'b0);
  not not_5 (not_5_out, 1'b0);
  not not_6 (not_6_out, 1'b0);
  not not_7 (not_7_out, 1'b0);
  not not_8 (not_8_out, 1'b0);
  not not_9 (not_9_out, 1'b0);
  Register #(.width(32)) PC (
    .D(multiplexer_1_out), .en(not_1_out), .Q({PC_q[31:26], PC_q_2, PC_q[1:0]}), .clk(CLK), .clr(1'b0));
  RAM #(.addrWidth(24), .dataWidth(32)) ram_1 (
    .addr(PC_q_2), .data(ram_1_data), .sel(not_3_out), .clk(CLK), .ld(not_2_out), .clr(1'b0));
  RAM #(.addrWidth(24), .dataWidth(32)) ram_2 (
    .addr(PC_q_2), .data(ram_2_data), .sel(not_4_out), .clk(CLK), .ld(not_5_out), .clr(1'b0));
  RAM #(.addrWidth(24), .dataWidth(32)) ram_3 (
    .addr(PC_q_2), .data(ram_3_data), .sel(not_7_out), .clk(CLK), .ld(not_6_out), .clr(1'b0));
  RAM #(.addrWidth(24), .dataWidth(32)) ram_4 (
    .addr(PC_q_2), .data(ram_4_data), .sel(not_9_out), .clk(CLK), .ld(not_8_out), .clr(1'b0));
  Adder #(.width(32)) adder_1 (
    .a(32'h4), .b({PC_q[31:26], PC_q_2, PC_q[1:0]}), .out(adder_1_out), .cin(1'b0));  // open: cout
  Multiplexer #(.select(2), .width(32)) multiplexer_2 (
    .in0(ram_1_data), .in1(ram_2_data), .in2(ram_3_data), .in3(ram_4_data), .out(INSTRUCTION),
    .sel(PC_q[27:26]), .en(1'b1));
endmodule

module REGFILE (
  input  RegWrite,
  input  clock,
  input  [4:0] RegWrite_2,
  output [31:0] ReadData1,
  output [31:0] ReadData2
);

  wire Wa0, Wa1, Wa2, Wa3, Wat, Wfp, Wgp, Wk0, Wk1, Wra, Ws0, Ws1, Ws2, Ws3, Ws4, Ws5, Ws6, Ws7, Wsp, Wt0,
       Wt1, Wt2, Wt3, Wt4, Wt5, Wt6, Wt7, Wt8, Wt9, Wv0, Wv1, WZero;
  wire [4:0] readRegister1_2_q, readRegister1_q;
  wire [31:0] a0, a1, a2, a3, at, fp, gp, k0, k1, ra, s0, s1, s2, s3, s4, s5, s6, s7, sp, t0, t1, t2, t3, t4,
       t5, t6, t7, t8, t9, v0, v1, Write_to_Register, Zero;

  Register #(.width(5)) readRegister1 (.Q(readRegister1_q), .clk(clock));  // open: D, en, clr
  Decoder #(.select(5), .disabled(0)) decoder_1 (
    .out0(WZero), .out1(Wat), .out2(Wv0), .out3(Wv1), .out4(Wa0), .out5(Wa1), .out6(Wa2), .out7(Wa3),
    .out8(Wt0), .out9(Wt1), .out10(Wt2), .out11(Wt3), .out12(Wt4), .out13(Wt5), .out14(Wt6), .out15(Wt7),
    .out16(Ws0), .out17(Ws1), .out18(Ws2), .out19(Ws3), .out20(Ws4), .out21(Ws5), .out22(Ws6), .out23(Ws7),
    .out24(Wt8), .out25(Wt9), .out26(Wk0), .out27(Wk1), .out28(Wgp), .out29(Wsp), .out30(Wfp), .out31(Wra),
    .sel(RegWrite_2), .en(RegWrite));
  Register #(.width(5)) readRegister1_2 (.Q(readRegister1_2_q), .clk(clock));  // open: D, en, clr
  Multiplexer #(.select(5), .width(32), .enable("false")) multiplexer_1 (
    .in0(Zero), .in1(at), .in2(v0), .in3(v1), .in4(a0), .in5(a1), .in6(a2), .in7(a3), .in8(t0), .in9(t1),
    .in10(t2), .in11(t3), .in12(t4), .in13(t5), .in14(t6), .in15(t7), .in16(s0), .in17(s1), .in18(s2),
    .in19(s3), .in20(s4), .in21(s5), .in22(s6), .in23(s7), .in24(t8), .in25(t9), .in26(k0), .in27(k1),
    .in28(gp), .in29(sp), .in30(fp), .in31(ra), .out(ReadData1), .sel(readRegister1_q));
  Multiplexer #(.select(5), .width(32), .enable("false")) multiplexer_2 (
    .in0(Zero), .in1(at), .in2(v0), .in3(v1), .in4(a0), .in5(a1), .in6(a2), .in7(a3), .in8(t0), .in9(t1),
    .in10(t2), .in11(t3), .in12(t4), .in13(t5), .in14(t6), .in15(t7), .in16(s0), .in17(s1), .in18(s2),
    .in19(s3), .in20(s4), .in21(s5), .in22(s6), .in23(s7), .in24(t8), .in25(t9), .in26(k0), .in27(k1),
    .in28(gp), .in29(sp), .in30(fp), .in31(ra), .out(ReadData2), .sel(readRegister1_2_q));
  Register #(.width(32)) writedata (.Q(Write_to_Register), .clk(clock));  // open: D, en, clr
  Register #(.width(32)) register_1 (.D(Write_to_Register), .en(Wv0), .Q(v0), .clk(clock));  // open: clr
  Register #(.width(32)) register_2 (.D(Write_to_Register), .en(Wv1), .Q(v1), .clk(clock));  // open: clr
  Register #(.width(32)) register_3 (.D(Write_to_Register), .en(WZero), .Q(Zero), .clk(clock));  // open: clr
  Register #(.width(32)) register_4 (.D(Write_to_Register), .en(Wa0), .Q(a0), .clk(clock));  // open: clr
  Register #(.width(32)) register_5 (.D(Write_to_Register), .en(Wa1), .Q(a1), .clk(clock));  // open: clr
  Register #(.width(32)) register_6 (.D(Write_to_Register), .en(Wa2), .Q(a2), .clk(clock));  // open: clr
  Register #(.width(32)) register_7 (.D(Write_to_Register), .en(Wa3), .Q(a3), .clk(clock));  // open: clr
  Register #(.width(32)) register_8 (.D(Write_to_Register), .en(Wt0), .Q(t0), .clk(clock));  // open: clr
  Register #(.width(32)) register_9 (.D(Write_to_Register), .en(Wt1), .Q(t1), .clk(clock));  // open: clr
  Register #(.width(32)) register_10 (.D(Write_to_Register), .en(Wt2), .Q(t2), .clk(clock));  // open: clr
  Register #(.width(32)) register_11 (.D(Write_to_Register), .en(Wt8), .Q(t8), .clk(clock));  // open: clr
  Register #(.width(32)) register_12 (.D(Write_to_Register), .en(Wt9), .Q(t9), .clk(clock));  // open: clr
  Register #(.width(32)) register_13 (.D(Write_to_Register), .en(Wk0), .Q(k0), .clk(clock));  // open: clr
  Register #(.width(32)) register_14 (.D(Write_to_Register), .en(Wk1), .Q(k1), .clk(clock));  // open: clr
  Register #(.width(32)) register_15 (.D(Write_to_Register), .en(Wgp), .Q(gp), .clk(clock));  // open: clr
  Register #(.width(32)) register_16 (.D(Write_to_Register), .en(Wfp), .Q(fp), .clk(clock));  // open: clr
  Register #(.width(32)) register_17 (.D(Write_to_Register), .en(Wat), .Q(at), .clk(clock));  // open: clr
  Register #(.width(32)) register_18 (.D(Write_to_Register), .en(Ws0), .Q(s0), .clk(clock));  // open: clr
  Register #(.width(32)) register_19 (.D(Write_to_Register), .en(Ws1), .Q(s1), .clk(clock));  // open: clr
  Register #(.width(32)) register_20 (.D(Write_to_Register), .en(Ws2), .Q(s2), .clk(clock));  // open: clr
  Register #(.width(32)) register_21 (.D(Write_to_Register), .en(Wt7), .Q(t7), .clk(clock));  // open: clr
  Register #(.width(32)) register_22 (.D(Write_to_Register), .en(Wt6), .Q(t6), .clk(clock));  // open: clr
  Register #(.width(32)) register_23 (.D(Write_to_Register), .en(Wt5), .Q(t5), .clk(clock));  // open: clr
  Register #(.width(32)) register_24 (.D(Write_to_Register), .en(Wt4), .Q(t4), .clk(clock));  // open: clr
  Register #(.width(32)) register_25 (.D(Write_to_Register), .en(Wt3), .Q(t3), .clk(clock));  // open: clr
  Register #(.width(32)) register_26 (.D(Write_to_Register), .en(Ws3), .Q(s3), .clk(clock));  // open: clr
  Register #(.width(32)) register_27 (.D(Write_to_Register), .en(Ws4), .Q(s4), .clk(clock));  // open: clr
  Register #(.width(32)) register_28 (.D(Write_to_Register), .en(Ws5), .Q(s5), .clk(clock));  // open: clr
  Register #(.width(32)) register_29 (.D(Write_to_Register), .en(Ws6), .Q(s6), .clk(clock));  // open: clr
  Register #(.width(32)) register_30 (.D(Write_to_Register), .en(Wra), .Q(ra), .clk(clock));  // open: clr
  Register #(.width(32)) register_31 (.D(Write_to_Register), .en(Ws7), .Q(s7), .clk(clock));  // open: clr
  Register #(.width(32)) register_32 (.D(Write_to_Register), .en(Wsp), .Q(sp), .clk(clock));  // open: clr

  // Other names for the same wires on the sheet: clk = clock
endmodule

module IF_ID (
  input  CLEAR,
  input  [31:0] INSTRUCTION,
  input  [31:0] PC,
  input  CLK,
  output [5:0] OPCODE,
  output [4:0] RS,
  output [4:0] RT,
  output [4:0] RD,
  output [4:0] SHAMT,
  output [5:0] FUNCT,
  output [15:0] IMMEDIATE,
  output [25:0] ADDRESS,
  output [31:0] PC_2
);

  wire not_1_out;

  Register #(.width(32)) u_instruction (
    .D(INSTRUCTION), .en(1'b1), .Q({OPCODE, ADDRESS}), .clk(not_1_out), .clr(CLEAR));
  Register #(.width(32)) program_counter (.D(PC), .en(1'b1), .Q(PC_2), .clk(not_1_out), .clr(CLEAR));
  not not_1 (not_1_out, CLK);

  assign FUNCT = ADDRESS[5:0];
  assign IMMEDIATE = ADDRESS[15:0];
  assign RD = ADDRESS[15:11];
  assign RS = ADDRESS[25:21];
  assign RT = ADDRESS[20:16];
  assign SHAMT = ADDRESS[10:6];
endmodule

module ID_EX (
  input  CLEAR,
  input  [31:0] PC,
  input  RegWrite,
  input  MemToReg,
  input  MemWrite,
  input  MemRead,
  input  Branch,
  input  [1:0] AluOp,
  input  RegDst,
  input  AluSrc,
  input  [31:0] ReadData1,
  input  [31:0] ReadData2,
  input  [31:0] Immediate,
  input  [4:0] RT,
  input  [4:0] RD,
  input  CLK,
  output [31:0] PC_2,
  output RegWrite_2,
  output MemToReg_2,
  output MemWrite_2,
  output MemRead_2,
  output Branch_2,
  output [1:0] AluOp_2,
  output RegDst_2,
  output AluSrc_2,
  output [31:0] ReadData1_2,
  output [31:0] ReadData2_2,
  output [31:0] IMMEADIATE,
  output [4:0] RT_2,
  output [4:0] RD_2
);

  wire not_1_out;

  not not_1 (not_1_out, CLK);
  Register #(.width(32)) program_counter (.D(PC), .en(1'b1), .Q(PC_2), .clk(not_1_out), .clr(CLEAR));
  Register #(.width(2)) wb (
    .D({RegWrite, MemToReg}), .en(1'b1), .Q({RegWrite_2, MemToReg_2}), .clk(not_1_out), .clr(CLEAR));
  Register #(.width(3)) mem (
    .D({MemWrite, MemRead, Branch}), .en(1'b1), .Q({MemWrite_2, MemRead_2, Branch_2}), .clk(not_1_out),
    .clr(CLEAR));
  Register #(.width(4)) ex (
    .D({AluOp, RegDst, AluSrc}), .en(1'b1), .Q({AluOp_2, RegDst_2, AluSrc_2}), .clk(not_1_out), .clr(CLEAR));
  Register #(.width(32)) read_data1 (.D(ReadData1), .en(1'b1), .Q(ReadData1_2), .clk(not_1_out), .clr(CLEAR));
  Register #(.width(32)) read_data2 (.D(ReadData2), .en(1'b1), .Q(ReadData2_2), .clk(not_1_out), .clr(CLEAR));
  Register #(.width(32)) u_immediate (.D(Immediate), .en(1'b1), .Q(IMMEADIATE), .clk(not_1_out), .clr(CLEAR));
  Register #(.width(5)) u_rt (.D(RT), .en(1'b1), .Q(RT_2), .clk(not_1_out), .clr(CLEAR));
  Register #(.width(5)) u_rd (.D(RD), .en(1'b1), .Q(RD_2), .clk(not_1_out), .clr(CLEAR));
endmodule
